# Fritzing sketch mpd (saved by Fritzing 0.9.3b)

parts:
  Raspberry_Pi_1 = Raspberry Pi 3 [part_number=RPI-3-V1.2]
  Grove1 = Grove OLED 128x96
  Part1 = KY-037 High Sensitivity Sound Detection Module [package="Breakout board"]
  J1 = STM32 Nucleo boards
  IC1 = Rasberry Pi NIOR Camera [chip_label=IC package="DIP (Dual Inline) [THT]"]  # not connected

nets:
  N1: Raspberry_Pi_1.GPIO2, Grove1.SDA
  N2: Raspberry_Pi_1.GPIO3, Grove1.SCL
  GND: Raspberry_Pi_1.GND, Grove1.GND
  5V: Raspberry_Pi_1.5V, Grove1.VCC
  N3: Part1.A0, J1.PA0
  N4: Part1.G, J1.GND
  N5: Part1.+, J1.5V

notes:
  Raspberry pi camera v2 slot

custom parts:
  KY-037 High Sensitivity Sound Detection Module: KY-037 high sensitivity sound detection module is an analog/digital sensor that uses a condenser microphone to observe changes in environment noise.
  Rasberry Pi NIOR Camera: Camera
